// Logisim project ex2.circ as structural Verilog: 1 circuit, main circuit AddMachine
module AddMachine (
  input  [7:0] in_1,
  output [7:0] ADD_OUT,
  output [7:0] REG_OUT
);

  wire clock_1_out;

  Adder adder_1 (.a(in_1), .b(REG_OUT), .out(ADD_OUT));  // open: cin, cout
  Clock clock_1 (.out(clock_1_out));
  Register register_1 (.D(ADD_OUT), .en(1'b1), .clk(clock_1_out), .Q(REG_OUT));  // open: clr

  // Notes on the sheet:
  //   PUT CIRCUITRY HERE
endmodule
