// Logisim project ex4.circ as structural Verilog: 1 circuit, main circuit Split
module Split (
  input  [7:0] In1,
  output Out1,
  output [7:0] Out2
);

  and and_1 (Out1, In1[0], In1[2]);

  assign Out2 = In1;
  // also tied to GND on the sheet: In1[1]

  // Notes on the sheet:
  //   PUT CIRCUITRY HERE
endmodule
