// Logisim project ex5.circ as structural Verilog: 5 circuits, main circuit rotr
module rotr (
  input  [15:0] A,
  input  [3:0] B,
  output [15:0] Out1
);

  wire [3:0] subtractor_1_out;
  wire [15:0] shifter_1_out, shifter_2_out;

  Subtractor #(.width(4)) subtractor_1 (.a(B), .b(4'b1111), .out(subtractor_1_out));  // open: bin, bout
  Shifter #(.shift("lr"), .width(16)) shifter_1 (.in(A), .\dist (B), .out(shifter_1_out));
  Shifter #(.width(16)) shifter_2 (.in(A), .\dist (subtractor_1_out), .out(shifter_2_out));
  assign Out1 = shifter_1_out | shifter_2_out;  // OR_Gate or_1, 16 bits wide

  // Notes on the sheet:
  //   PUT CIRCUITRY HERE
endmodule

module rot8 (
  input  [15:0] in_1,
  output [15:0] out_2
);


  // Notes on the sheet:
  //   PUT CIRCUITRY HERE
endmodule

module rot4 (
  input  [15:0] in_1,
  output [15:0] out_2
);


  // Notes on the sheet:
  //   PUT CIRCUITRY HERE
endmodule

module rot2 (
  input  [15:0] in_1,
  output [15:0] out_2
);


  // Notes on the sheet:
  //   PUT CIRCUITRY HERE
endmodule

module rot1 (
  input  [15:0] in_1,
  output [15:0] out_2
);


  // Notes on the sheet:
  //   PUT CIRCUITRY HERE
endmodule
