// Logisim project control_logic.circ as structural Verilog: 1 circuit, main circuit control_logic
module control_logic (
  input  [31:0] inst,
  input  BrEq,
  input  BrLt,
  output PCSel,
  output RegWEn,
  output [2:0] ImmSel,
  output BrUn,
  output ASel,
  output BSel,
  output [3:0] ALUSel,
  output MemRW,
  output [1:0] WBSel,
  output CSRSel,
  output CSRWen,
  output [3:0] MemUnit
);

  wire and_2_out, and_3_out, and_8_out, and_10_out, and_11_out, and_14_out, and_15_out, and_16_out,
       and_18_out, and_19_out, and_20_out, and_21_out, and_22_out, and_23_out, and_24_out, and_25_out,
       and_26_out, and_28_out, and_33_out, and_34_out, and_35_out, and_37_out, and_38_out, and_39_out,
       and_40_out, and_41_out, and_42_out, and_43_out, and_47_out, and_48_out, and_49_out, and_50_out,
       and_51_out, and_52_out, and_53_out, and_54_out, and_55_out, and_57_out, and_59_out, and_60_out,
       and_61_out, and_63_out, and_64_out, and_65_out, and_67_out, and_68_out, and_69_out, and_70_out,
       ASel_error_old, auipc_inst, B_Type, B_Type_PCSel, BSel_old, CSRWen_old, I_Type, I_Type_ALUSel_0,
       I_Type_ALUSel_1, I_Type_ALUSel_2, imm_0, imm_1, imm_2, jalr_inst, load_inst, lui_inst, MemRW_old,
       or_10_out, or_11_out, or_12_out, or_16_out, or_18_out, or_20_out, or_21_out, or_23_out, or_24_out,
       or_26_out, or_27_out, PCSel_old, R_Type, R_Type_ALUSel_0, R_Type_ALUSel_1, R_Type_ALUSel_2,
       R_Type_ALUSel_3, RegWEn_old, WBSel_0_old, WBSel_1_old, xnor_1_out, xnor_2_out, xor_1_out, xor_2_out,
       xor_3_out, xor_4_out, xor_5_out, xor_6_out, xor_7_out, xor_8_out;

  or or_1 (ASel, B_Type, auipc_inst, ImmSel[2]);
  or or_2 (WBSel[1], jalr_inst, ImmSel[2]);
  xor xor_1 (xor_1_out, inst[12], BrEq);
  xor xor_2 (xor_2_out, BrLt, inst[12]);
  and and_1 (MemUnit[3], ~inst[12], inst[13], ~inst[14]);  // AND_Gate
  and and_2 (and_2_out, ~inst[14], ~inst[13], xor_1_out);  // AND_Gate
  and and_3 (and_3_out, inst[14], xor_2_out);
  not not_1 (BSel, R_Type);
  or or_3 (ImmSel[1], lui_inst, auipc_inst, B_Type);
  or or_4 (MemUnit[1], inst[12], inst[13], inst[14]);
  or or_5 (B_Type_PCSel, and_2_out, and_3_out);
  or or_6 (WBSel[0], R_Type, I_Type, auipc_inst, lui_inst);
  and and_4 (RegWEn, ~CSRWen, ~MemRW, ~B_Type);  // AND_Gate
  and and_5 (CSRSel, inst[14], ~inst[13], inst[12]);  // AND_Gate
  and and_6 (WBSel_1_old, inst[6], inst[5], ~inst[4], inst[2]);  // AND_Gate
  and and_7 (WBSel_0_old, ~inst[6], inst[4], ~inst[3]);  // AND_Gate
  or or_7 (ImmSel[0], lui_inst, auipc_inst, MemRW);
  or or_8 (BSel_old, inst[6], ~inst[5], ~inst[4], inst[3], inst[2]);  // OR_Gate
  and and_8 (and_8_out, B_Type, B_Type_PCSel);
  and and_9 (BrUn, inst[14], inst[13]);
  or or_9 (PCSel, and_8_out, ImmSel[2], jalr_inst);
  and and_10 (and_10_out, inst[6], inst[5], ~inst[4]);  // AND_Gate
  and and_11 (and_11_out, ~inst[6], ~inst[5], inst[4], ~inst[3]);  // AND_Gate
  or or_10 (or_10_out, and_10_out, and_11_out);
  and and_12 (ASel_error_old, or_10_out, inst[2]);
  and and_13 (MemRW_old, ~inst[6], inst[5], ~inst[4], ~inst[3], ~inst[2]);  // AND_Gate
  and and_14 (and_14_out, ~inst[6], ~inst[3], ~inst[2]);  // AND_Gate
  and and_15 (and_15_out, ~inst[5], and_14_out);  // AND_Gate
  and and_16 (and_16_out, and_14_out, inst[5]);
  and and_17 (R_Type, inst[4], and_16_out);
  xor xor_3 (xor_3_out, inst[30], inst[25]);
  and and_18 (and_18_out, ~inst[14], ~inst[13], ~inst[12]);  // AND_Gate
  and and_19 (and_19_out, inst[13], ~inst[30]);  // AND_Gate
  xor xor_4 (xor_4_out, inst[13], inst[12]);
  and and_20 (and_20_out, xor_3_out, ~inst[13], ~inst[12]);  // AND_Gate
  and and_21 (and_21_out, inst[12], ~inst[30], inst[25]);  // AND_Gate
  or or_11 (or_11_out, ~inst[13], and_19_out);  // OR_Gate
  and and_22 (and_22_out, xor_4_out, ~inst[14]);  // AND_Gate
  and and_23 (and_23_out, ~inst[13], inst[12], inst[14]);  // AND_Gate
  and and_24 (and_24_out, R_Type, R_Type_ALUSel_3);
  and and_25 (and_25_out, I_Type, 1'b0);
  and and_26 (and_26_out, ~inst[6], inst[4]);  // AND_Gate
  and and_27 (MemRW, ~inst[4], and_16_out);  // AND_Gate
  or or_12 (or_12_out, and_20_out, and_21_out);
  and and_28 (and_28_out, or_11_out, inst[14], inst[12]);
  or or_13 (I_Type_ALUSel_2, and_22_out, and_23_out);
  or or_14 (ALUSel[3], and_24_out, and_25_out, lui_inst);
  or or_15 (RegWEn_old, and_26_out, ~inst[5], inst[3], inst[2]);  // OR_Gate
  and and_29 (CSRWen_old, inst[6], inst[5], inst[4], ~inst[3], ~inst[2]);  // AND_Gate
  and and_30 (I_Type, inst[4], and_15_out);
  or or_16 (or_16_out, and_18_out, and_28_out);
  and and_31 (load_inst, ~inst[4], and_15_out);  // AND_Gate
  and and_32 (R_Type_ALUSel_3, ~inst[14], or_12_out);  // AND_Gate
  nand nand_1 (R_Type_ALUSel_1, or_16_out, ~inst[25]);  // NAND_Gate
  and and_33 (and_33_out, R_Type, R_Type_ALUSel_2);
  and and_34 (and_34_out, I_Type, I_Type_ALUSel_2);
  and and_35 (and_35_out, inst[6], inst[5]);
  xor xor_5 (xor_5_out, inst[13], inst[12]);
  or or_17 (ALUSel[2], and_33_out, and_34_out, lui_inst);
  and and_36 (imm_2, inst[6], inst[5], ~inst[4], inst[3], inst[2]);  // AND_Gate
  and and_37 (and_37_out, inst[5], ~inst[4], ~inst[2]);  // AND_Gate
  and and_38 (and_38_out, inst[4], inst[2]);
  xor xor_6 (xor_6_out, inst[12], BrEq);
  xor xor_7 (xor_7_out, BrLt, inst[12]);
  and and_39 (and_39_out, ~inst[4], ~inst[3], and_35_out);  // AND_Gate
  and and_40 (and_40_out, xor_5_out, ~inst[14]);  // AND_Gate
  and and_41 (and_41_out, ~inst[12], inst[14]);  // AND_Gate
  or or_18 (or_18_out, and_37_out, and_38_out);
  and and_42 (and_42_out, ~inst[14], ~inst[13], xor_6_out);  // AND_Gate
  and and_43 (and_43_out, inst[14], xor_7_out);
  and and_44 (B_Type, ~inst[2], and_39_out);  // AND_Gate
  xnor xnor_1 (xnor_1_out, inst[12], inst[25]);
  or or_19 (I_Type_ALUSel_1, and_40_out, and_41_out);
  and and_45 (imm_0, ~inst[3], or_18_out, ~inst[6]);  // AND_Gate
  or or_20 (or_20_out, and_42_out, and_43_out);
  and and_46 (jalr_inst, inst[2], and_39_out);
  and and_47 (and_47_out, inst[12], ~inst[30]);  // AND_Gate
  and and_48 (and_48_out, ~inst[12], inst[30], ~inst[25]);  // AND_Gate
  and and_49 (and_49_out, ~inst[14], inst[13], ~inst[12], ~inst[30], ~inst[25]);  // AND_Gate
  and and_50 (and_50_out, xnor_1_out, ~inst[14], inst[13], ~inst[30]);  // AND_Gate
  and and_51 (and_51_out, R_Type, R_Type_ALUSel_1);
  and and_52 (and_52_out, I_Type, I_Type_ALUSel_1);
  and and_53 (and_53_out, inst[6], inst[5], ~inst[4], ~inst[2]);  // AND_Gate
  and and_54 (and_54_out, ~inst[6], inst[4], inst[2]);  // AND_Gate
  or or_21 (or_21_out, and_47_out, and_48_out);
  or or_22 (ALUSel[1], and_51_out, and_52_out);
  and and_55 (and_55_out, ~inst[3], ~inst[2], or_20_out);  // AND_Gate
  and and_56 (CSRWen, and_35_out, ~inst[2], ~inst[3], inst[4]);  // AND_Gate
  and and_57 (and_57_out, or_21_out, ~inst[14], ~inst[13]);  // AND_Gate
  xnor xnor_2 (xnor_2_out, inst[12], inst[30]);
  or or_23 (or_23_out, and_53_out, and_54_out);
  and and_58 (ImmSel[2], and_35_out, inst[2], inst[3], ~inst[4]);  // AND_Gate
  and and_59 (and_59_out, inst[14], ~inst[13], inst[12], ~inst[25]);  // AND_Gate
  and and_60 (and_60_out, xnor_2_out, ~inst[13]);  // AND_Gate
  and and_61 (and_61_out, inst[13], inst[12], ~inst[30]);  // AND_Gate
  and and_62 (imm_1, or_23_out, ~inst[3]);  // AND_Gate
  or or_24 (or_24_out, and_55_out, inst[2]);
  or or_25 (R_Type_ALUSel_2, and_57_out, and_59_out, and_49_out);
  xor xor_8 (xor_8_out, inst[14], inst[13]);
  and and_63 (and_63_out, ~inst[13], inst[30]);  // AND_Gate
  and and_64 (and_64_out, R_Type, R_Type_ALUSel_0);
  and and_65 (and_65_out, I_Type, I_Type_ALUSel_0);
  and and_66 (PCSel_old, or_24_out, inst[6], inst[5], ~inst[4]);  // AND_Gate
  or or_26 (or_26_out, and_60_out, and_61_out);
  and and_67 (and_67_out, xor_8_out, ~inst[12]);  // AND_Gate
  or or_27 (or_27_out, inst[13], and_63_out);
  or or_28 (ALUSel[0], and_64_out, and_65_out, lui_inst);
  and and_68 (and_68_out, ~inst[6], inst[4], ~inst[3], inst[2]);  // AND_Gate
  and and_69 (and_69_out, inst[14], or_26_out, ~inst[25]);  // AND_Gate
  and and_70 (and_70_out, inst[14], inst[12], or_27_out);
  and and_71 (auipc_inst, ~inst[5], and_68_out);  // AND_Gate
  or or_29 (R_Type_ALUSel_0, and_69_out, and_50_out);
  or or_30 (I_Type_ALUSel_0, and_67_out, and_70_out);
  and and_72 (lui_inst, inst[5], and_68_out);

  assign {MemUnit[2], MemUnit[0]} = {MemUnit[3], 1'b1};

  // Other names for the same wires on the sheet: ALUSel_0 = ALUSel[0]; ALUSel_1 = ALUSel[1]; ALUSel_2 = ALUSel[2];
  //   ALUSel_3 = ALUSel[3]; csr_inst = CSRWen; ImmSel_0 = ImmSel[0]; ImmSel_1 = ImmSel[1]; ImmSel_2 = ImmSel[2];
  //   J_Type = ImmSel[2]; ImmSel_old[2:0] = {imm_2, imm_1, imm_0}; op_0 = inst[0]; opcode[6:0] = inst[6:0];
  //   op_1 = inst[1]; op_2 = inst[2]; op_3 = inst[3]; op_4 = inst[4]; op_5 = inst[5]; op_6 = inst[6];
  //   fn3_0 = inst[12]; funct3[2:0] = inst[14:12]; fn3_1 = inst[13]; fn3_2 = inst[14]; fn7_0 = inst[25];
  //   funct7[6:0] = inst[31:25]; fn7_1 = inst[26]; fn7_2 = inst[27]; fn7_3 = inst[28]; fn7_4 = inst[29];
  //   fn7_5 = inst[30]; fn7_6 = inst[31]; MemUnit_1 = MemUnit[1]; MemUnit_2 = MemUnit[3]; MemUnit_3 = MemUnit[3];
  //   S_Type = MemRW; WBSel_0 = WBSel[0]; WBSel_old[1:0] = WBSel; WBSel_1 = WBSel[1]

  // Notes on the sheet:
  //   INPUTS to your circuit
  //   Memory Unit: 1111-w, 0011-h, 0001-b
  //   Control Status Register (CSR)
  //   DON'T CHANGE THE LOCATIONS OF THE INPUTS AND OUTPUTS!
  //   OUTPUT from your circuit
  //   ImmSel: 0:I-type, 1:S-type, 2:B-type, 3:U-type, 4:J-type
  //   CSRSel: 0:rs1, 1:imm
  //   old version
  //   ImmSel: 0:I-type, 1:S-type, 2:B-type, 3:U-type, 4:J-type
endmodule
