// Logisim project cpu.circ as structural Verilog: 1 circuit, main circuit cpu
module cpu (
  input  clk,
  input  [31:0] INSTRUCTION,
  input  [31:0] READ_DATA,
  output [31:0] WRITE_ADDRESS,
  output [31:0] PROGRAM_COUNTER,
  output [31:0] ra,
  output [31:0] sp,
  output [31:0] t0,
  output [31:0] t1,
  output [31:0] t2,
  output [31:0] s0,
  output [31:0] s1,
  output [31:0] a0,
  output [31:0] tohost,
  output [3:0] WRITE_ENABLE,
  output [31:0] WRITE_DATA
);

  wire ASel, BrEq, BrLt, BrUn, BSel, CSRSel, CSRWen, MemRW, PCSel, RegWEn;
  wire [1:0] WBSel;
  wire [2:0] ImmSel;
  wire [3:0] ALUSel, MemUnit;
  wire [31:0] adder_1_out, Aoprand, bit_extender_1_out, bit_extender_2_out, bit_extender_3_out, Boprand,
       CSRWData, data_rs1, imm, Inst_EX, LOAD_DATA, multiplexer_1_out, multiplexer_2_out, PC_EX, Return_addr,
       WBData;

  Adder #(.width(32)) adder_1 (.a(PROGRAM_COUNTER), .b(32'h4), .out(adder_1_out));  // open: cin, cout
  Register #(.width(32)) PC (.D(multiplexer_1_out), .clk(clk), .Q(PROGRAM_COUNTER));  // open: en, clr
  Multiplexer #(.enable("false"), .width(32)) multiplexer_1 (
    .in0(adder_1_out), .in1(WRITE_ADDRESS), .out(multiplexer_1_out), .sel(PCSel));
  Multiplexer #(.enable("false"), .width(32)) multiplexer_2 (
    .in0(INSTRUCTION), .in1(32'h13), .out(multiplexer_2_out), .sel(PCSel));
  Register #(.width(32)) PC_IF_EC_reg (.D(PROGRAM_COUNTER), .clk(clk), .Q(PC_EX));  // open: en, clr
  Register #(.width(32)) Inst_IF_EC_reg (.D(multiplexer_2_out), .clk(clk), .Q(Inst_EX));  // open: en, clr
  control_logic control_logic_1 (
    .CSRWen(CSRWen), .MemUnit(MemUnit), .PCSel(PCSel), .RegWEn(RegWEn), .ImmSel(ImmSel), .BrUn(BrUn),
    .ASel(ASel), .BSel(BSel), .ALUSel(ALUSel), .MemRW(MemRW), .WBSel(WBSel), .CSRSel(CSRSel), .inst(Inst_EX),
    .BrEq(BrEq), .BrLt(BrLt));
  regfile regfile_1 (
    .rs1(Inst_EX[19:15]), .rs2(Inst_EX[24:20]), .rd(Inst_EX[11:7]), .Write_Data(WBData), .RegWEn(RegWEn),
    .clk(clk), .ra(ra), .sp(sp), .t0(t0), .t1(t1), .t2(t2), .s0(s0), .s1(s1), .a0(a0),
    .Read_Data_1(data_rs1), .Read_Data_2(WRITE_DATA));
  imm_gen imm_gen_1 (.inst(Inst_EX), .ImmSel(ImmSel), .imm(imm));
  Multiplexer #(.enable("false"), .width(32)) multiplexer_3 (.in0(data_rs1), .in1(PC_EX), .out(Aoprand), .sel(ASel));
  Multiplexer #(.enable("false"), .width(32)) multiplexer_4 (.in0(WRITE_DATA), .in1(imm), .out(Boprand), .sel(BSel));
  branch_comp branch_comp_1 (.rs1(data_rs1), .rs2(WRITE_DATA), .BrUn(BrUn), .BrEq(BrEq), .BrLt(BrLt));
  alu alu_1 (.A(Aoprand), .B(Boprand), .ALUSel(ALUSel), .Result(WRITE_ADDRESS));
  and and_1 (WRITE_ENABLE[3], MemUnit[3], MemRW);
  and and_2 (WRITE_ENABLE[2], MemUnit[2], MemRW);
  and and_3 (WRITE_ENABLE[1], MemUnit[1], MemRW);
  and and_4 (WRITE_ENABLE[0], MemUnit[0], MemRW);
  Adder #(.width(32)) adder_2 (.a(PC_EX), .b(32'h4), .out(Return_addr));  // open: cin, cout
  Multiplexer #(.enable("false"), .select(2), .width(32)) multiplexer_5 (
    .in0(LOAD_DATA), .in1(WRITE_ADDRESS), .in2(Return_addr), .out(WBData), .sel(WBSel));  // open: in3
  assign bit_extender_1_out = {{27{1'b0}}, Inst_EX[19:15]};  // Bit_Extender bit_extender_1
  assign bit_extender_2_out = {{24{READ_DATA[7]}}, READ_DATA[7:0]};  // Bit_Extender bit_extender_2
  assign bit_extender_3_out = {{16{READ_DATA[15]}}, READ_DATA[15:0]};  // Bit_Extender bit_extender_3
  Multiplexer #(.enable("false"), .width(32)) multiplexer_6 (
    .in0(data_rs1), .in1(bit_extender_1_out), .out(CSRWData), .sel(CSRSel));
  Multiplexer #(.enable("false"), .select(2), .width(32)) multiplexer_7 (
    .in0(bit_extender_2_out), .in1(bit_extender_3_out), .in3(READ_DATA), .out(LOAD_DATA), .sel(MemUnit[2:1]));  // open: in2
  csr csr_1 (.CSR_address(imm[11:0]), .CSR_din(CSRWData), .CSR_WE(CSRWen), .clk(clk), .tohost(tohost));

  // Other names for the same wires on the sheet: ALUResult[31:0] = WRITE_ADDRESS; data_rs2[31:0] = WRITE_DATA;
  //   rd[4:0] = Inst_EX[11:7]; rs1[4:0] = Inst_EX[19:15]; rs2[4:0] = Inst_EX[24:20]

  // Notes on the sheet:
  //   Output to IMEM
  //   IMEM (do **NOT** move this)
  //   Inputs from IMEM
  //   It is OK to move the PC, RegFile, ALU, MEM, Branch Comp, Imm Gen, and Control Logic to wherever is most convenient for you when constructing your CPU, and to delete this text
  //   Inputs/Outputs for testing. Do **NOT** move these.
  //   Outputs To DMEM
  //   DMEM (do **NOT** move this)
  //   Inputs From DMEM
endmodule
