// Logisim project imm_gen.circ as structural Verilog: 1 circuit, main circuit imm_gen
module imm_gen (
  input  [31:0] inst,
  input  [2:0] ImmSel,
  output [31:0] imm
);

  wire [31:0] b_type_imm, i_type_imm, j_type_imm, s_type_imm;

  assign i_type_imm = {{20{inst[31]}}, inst[31:20]};  // Bit_Extender bit_extender_1
  assign s_type_imm = {{20{inst[31]}}, {inst[31:25], inst[11:7]}};  // Bit_Extender bit_extender_2
  assign b_type_imm = {{19{inst[31]}}, {inst[31], inst[7], inst[30:25], inst[11:8], 1'b0}};  // Bit_Extender bit_extender_3
  assign j_type_imm = {{11{inst[31]}}, {inst[31], inst[19:12], inst[20], inst[30:21], 1'b0}};  // Bit_Extender bit_extender_4
  Multiplexer #(.enable("false"), .select(3), .width(32)) multiplexer_1 (
    .in0(i_type_imm), .in1(s_type_imm), .in2(b_type_imm), .in3({inst[31:12], {12{1'b0}}}), .in4(j_type_imm),
    .out(imm), .sel(ImmSel));  // open: in5, in6, in7

  // Other names for the same wires on the sheet: u_type_imm[31:12] = inst[31:12]

  // Notes on the sheet:
  //   INPUTS to your circuit
  //   DON'T CHANGE THE LOCATIONS OF THE INPUTS AND OUTPUTS!
  //   0: I-Type
  //   0: I-Type, 1: S-Type, 2: B-Type, 3: U-Type, 4: J-Type
  //   OUTPUT from your circuit
endmodule
