// Logisim project regfile.circ as structural Verilog: 1 circuit, main circuit regfile
module regfile (
  input  [4:0] rs1,
  input  [4:0] rs2,
  input  [4:0] rd,
  input  [31:0] Write_Data,
  input  RegWEn,
  input  clk,
  output [31:0] ra,
  output [31:0] sp,
  output [31:0] t0,
  output [31:0] t1,
  output [31:0] t2,
  output [31:0] s0,
  output [31:0] s1,
  output [31:0] a0,
  output [31:0] Read_Data_1,
  output [31:0] Read_Data_2
);

  wire [7:0] WEn0_7, WEn8_15, WEn16_23, WEn24_31;
  wire [31:0] x3, x4, x11, x12, x13, x14, x15, x16, x17, x18, x19, x20, x21, x22, x23, x24, x25, x26, x27,
       x28, x29, x30, x31;

  Multiplexer #(.enable("false"), .select(5), .width(32)) multiplexer_1 (
    .in0({32{1'b0}}), .in1(ra), .in2(sp), .in3(x3), .in4(x4), .in5(t0), .in6(t1), .in7(t2), .in8(s0),
    .in9(s1), .in10(a0), .in11(x11), .in12(x12), .in13(x13), .in14(x14), .in15(x15), .in16(x16), .in17(x17),
    .in18(x18), .in19(x19), .in20(x20), .in21(x21), .in22(x22), .in23(x23), .in24(x24), .in25(x25),
    .in26(x26), .in27(x27), .in28(x28), .in29(x29), .in30(x30), .in31(x31), .out(Read_Data_1), .sel(rs1));
  Demultiplexer #(.select(5)) demultiplexer_1 (
    .out0(WEn0_7[0]), .out1(WEn0_7[1]), .out2(WEn0_7[2]), .out3(WEn0_7[3]), .out4(WEn0_7[4]),
    .out5(WEn0_7[5]), .out6(WEn0_7[6]), .out7(WEn0_7[7]), .out8(WEn8_15[0]), .out9(WEn8_15[1]),
    .out10(WEn8_15[2]), .out11(WEn8_15[3]), .out12(WEn8_15[4]), .out13(WEn8_15[5]), .out14(WEn8_15[6]),
    .out15(WEn8_15[7]), .out16(WEn16_23[0]), .out17(WEn16_23[1]), .out18(WEn16_23[2]), .out19(WEn16_23[3]),
    .out20(WEn16_23[4]), .out21(WEn16_23[5]), .out22(WEn16_23[6]), .out23(WEn16_23[7]), .out24(WEn24_31[0]),
    .out25(WEn24_31[1]), .out26(WEn24_31[2]), .out27(WEn24_31[3]), .out28(WEn24_31[4]), .out29(WEn24_31[5]),
    .out30(WEn24_31[6]), .out31(WEn24_31[7]), .in(1'b1), .sel(rd), .en(RegWEn));
  Multiplexer #(.enable("false"), .select(5), .width(32)) multiplexer_2 (
    .in0({32{1'b0}}), .in1(ra), .in2(sp), .in3(x3), .in4(x4), .in5(t0), .in6(t1), .in7(t2), .in8(s0),
    .in9(s1), .in10(a0), .in11(x11), .in12(x12), .in13(x13), .in14(x14), .in15(x15), .in16(x16), .in17(x17),
    .in18(x18), .in19(x19), .in20(x20), .in21(x21), .in22(x22), .in23(x23), .in24(x24), .in25(x25),
    .in26(x26), .in27(x27), .in28(x28), .in29(x29), .in30(x30), .in31(x31), .out(Read_Data_2), .sel(rs2));
  Register #(.width(32)) u_x4 (.D(Write_Data), .en(WEn0_7[4]), .clk(clk), .Q(x4));  // open: clr
  Register #(.width(32)) x8 (.D(Write_Data), .en(WEn8_15[0]), .clk(clk), .Q(s0));  // open: clr
  Register #(.width(32)) u_x12 (.D(Write_Data), .en(WEn8_15[4]), .clk(clk), .Q(x12));  // open: clr
  Register #(.width(32)) u_x16 (.D(Write_Data), .en(WEn16_23[0]), .clk(clk), .Q(x16));  // open: clr
  Register #(.width(32)) u_x20 (.D(Write_Data), .en(WEn16_23[4]), .clk(clk), .Q(x20));  // open: clr
  Register #(.width(32)) u_x24 (.D(Write_Data), .en(WEn24_31[0]), .clk(clk), .Q(x24));  // open: clr
  Register #(.width(32)) u_x28 (.D(Write_Data), .en(WEn24_31[4]), .clk(clk), .Q(x28));  // open: clr
  Register #(.width(32)) x1 (.D(Write_Data), .en(WEn0_7[1]), .clk(clk), .Q(ra));  // open: clr
  Register #(.width(32)) x5 (.D(Write_Data), .en(WEn0_7[5]), .clk(clk), .Q(t0));  // open: clr
  Register #(.width(32)) x9 (.D(Write_Data), .en(WEn8_15[1]), .clk(clk), .Q(s1));  // open: clr
  Register #(.width(32)) u_x13 (.D(Write_Data), .en(WEn8_15[5]), .clk(clk), .Q(x13));  // open: clr
  Register #(.width(32)) u_x17 (.D(Write_Data), .en(WEn16_23[1]), .clk(clk), .Q(x17));  // open: clr
  Register #(.width(32)) u_x21 (.D(Write_Data), .en(WEn16_23[5]), .clk(clk), .Q(x21));  // open: clr
  Register #(.width(32)) u_x25 (.D(Write_Data), .en(WEn24_31[1]), .clk(clk), .Q(x25));  // open: clr
  Register #(.width(32)) u_x29 (.D(Write_Data), .en(WEn24_31[5]), .clk(clk), .Q(x29));  // open: clr
  Register #(.width(32)) x2 (.D(Write_Data), .en(WEn0_7[2]), .clk(clk), .Q(sp));  // open: clr
  Register #(.width(32)) x6 (.D(Write_Data), .en(WEn0_7[6]), .clk(clk), .Q(t1));  // open: clr
  Register #(.width(32)) x10 (.D(Write_Data), .en(WEn8_15[2]), .clk(clk), .Q(a0));  // open: clr
  Register #(.width(32)) u_x14 (.D(Write_Data), .en(WEn8_15[6]), .clk(clk), .Q(x14));  // open: clr
  Register #(.width(32)) u_x18 (.D(Write_Data), .en(WEn16_23[2]), .clk(clk), .Q(x18));  // open: clr
  Register #(.width(32)) u_x22 (.D(Write_Data), .en(WEn16_23[6]), .clk(clk), .Q(x22));  // open: clr
  Register #(.width(32)) u_x26 (.D(Write_Data), .en(WEn24_31[2]), .clk(clk), .Q(x26));  // open: clr
  Register #(.width(32)) u_x30 (.D(Write_Data), .en(WEn24_31[6]), .clk(clk), .Q(x30));  // open: clr
  Register #(.width(32)) u_x3 (.D(Write_Data), .en(WEn0_7[3]), .clk(clk), .Q(x3));  // open: clr
  Register #(.width(32)) x7 (.D(Write_Data), .en(WEn0_7[7]), .clk(clk), .Q(t2));  // open: clr
  Register #(.width(32)) u_x11 (.D(Write_Data), .en(WEn8_15[3]), .clk(clk), .Q(x11));  // open: clr
  Register #(.width(32)) u_x15 (.D(Write_Data), .en(WEn8_15[7]), .clk(clk), .Q(x15));  // open: clr
  Register #(.width(32)) u_x19 (.D(Write_Data), .en(WEn16_23[3]), .clk(clk), .Q(x19));  // open: clr
  Register #(.width(32)) u_x23 (.D(Write_Data), .en(WEn16_23[7]), .clk(clk), .Q(x23));  // open: clr
  Register #(.width(32)) u_x27 (.D(Write_Data), .en(WEn24_31[3]), .clk(clk), .Q(x27));  // open: clr
  Register #(.width(32)) u_x31 (.D(Write_Data), .en(WEn24_31[7]), .clk(clk), .Q(x31));  // open: clr

  // Other names for the same wires on the sheet: read_data1[31:0] = Read_Data_1; read_data2[31:0] = Read_Data_2;
  //   read_reg1[4:0] = rs1; read_reg2[4:0] = rs2; write_en_x0 = WEn0_7[0]; write_en_x1 = WEn0_7[1];
  //   write_en_x2 = WEn0_7[2]; write_en_x3 = WEn0_7[3]; write_en_x4 = WEn0_7[4]; write_en_x5 = WEn0_7[5];
  //   write_en_x6 = WEn0_7[6]; write_en_x7 = WEn0_7[7]; write_en_x8 = WEn8_15[0]; write_en_x9 = WEn8_15[1];
  //   write_en_x10 = WEn8_15[2]; write_en_x11 = WEn8_15[3]; write_en_x12 = WEn8_15[4]; write_en_x13 = WEn8_15[5];
  //   write_en_x14 = WEn8_15[6]; write_en_x15 = WEn8_15[7]; write_en_x16 = WEn16_23[0]; write_en_x17 = WEn16_23[1];
  //   write_en_x18 = WEn16_23[2]; write_en_x19 = WEn16_23[3]; write_en_x20 = WEn16_23[4]; write_en_x21 = WEn16_23[5];
  //   write_en_x22 = WEn16_23[6]; write_en_x23 = WEn16_23[7]; write_en_x24 = WEn24_31[0]; write_en_x25 = WEn24_31[1];
  //   write_en_x26 = WEn24_31[2]; write_en_x27 = WEn24_31[3]; write_en_x28 = WEn24_31[4]; write_en_x29 = WEn24_31[5];
  //   write_en_x30 = WEn24_31[6]; write_en_x31 = WEn24_31[7]; write_en = RegWEn; write_reg[4:0] = rd; x1[31:0] = ra;
  //   x2[31:0] = sp; x5[31:0] = t0; x6[31:0] = t1; x7[31:0] = t2; x8[31:0] = s0; x9[31:0] = s1; x10[31:0] = a0

  // Notes on the sheet:
  //   INPUTS to your circuit
  //   select read_data1
  //   DON'T CHANGE THE LOCATIONS OF THE INPUTS AND OUTPUTS!
  //   These are DEBUG/TEST outputs from your circuit.
  //   demultiplex write_reg
  //   select read_data2
  //   Alias
  //   OUTPUTS from your circuit
  //   Registers
endmodule
