// Logisim project cpu-integration-test-proj2-all-func.circ as structural Verilog: 1 circuit, main circuit run_main
module run_main (
  output [31:0] ra,
  output [31:0] sp,
  output [31:0] t0,
  output [31:0] t1,
  output [31:0] t2,
  output [31:0] s0,
  output [31:0] s1,
  output [31:0] a0,
  output [31:0] Requested_Address,
  output [31:0] Requested_Instruction,
  output [15:0] Time_Step,
  output halt
);

  wire clk;

  Clock clock_1 (.out(clk));
  // Probe on Requested_Address
  // test_harness test_harness_1: pin names not known; wires that end beside it: Requested_Instruction, clk, Requested_Address, ra, sp, t0, t1, t2, s0, s1, a0
  ROM #(.addrWidth(14), .dataWidth(32)) rom_1 (.addr(Requested_Address[15:2]), .data(Requested_Instruction));
  // Probe on Requested_Instruction
  Counter #(.max('hffff), .width(16)) counter_1 (.clk(clk), .Q(Time_Step));  // open: clr, load, up, count, D, carry
  Comparator #(.width(16)) comparator_1 (.a(Time_Step), .b(16'h6b8), .eq(halt));  // open: gt, lt

  // Other names for the same wires on the sheet: fetch_addr[31:0] = Requested_Address;
  //   Instruction[31:0] = Requested_Instruction

  // Notes on the sheet:
  //   contents of rom_1 (hex, n*v repeats v):
  //   00001437 FF040413 FF700293 00542023 00500293 00542223 00900293 00542423 FFD00293 00542623 01800293
  //   00542823 02400293 00542A23 06600293 00542C23 04D00293 00542E23 F8500293 02542023 01700293 02542223
  //   03400293 02542423 05700293 02542623 03040493 FFD00293 0054A023 00F00293 0054A223 01800293 0054A423
  //   02400293 0054A623 00D00293 0054A823 02300293 0054AA23 08E00293 0054AC23 30300293 0054AE23 F9900293
  //   0254A023 01B00293 0254A223 02600293 0254A423 03900293 0254A623 03048913 00040513 00400593 00300613
  //   00048693 00300713 00400793 00090813 00000317 07C300E7 00092283 00492283 00892283 00C92283 01092283
  //   01492283 01892283 01C92283 02092283 02492283 00090513 00900593 00000317 20C300E7 00090513 00900593
  //   00000317 248300E7 00092283 00492283 00892283 00C92283 01092283 01492283 01892283 01C92283 02092283
  //   02492283 2540006F 00100293 0055D663 04800593 2440006F 00565663 04800593 2380006F 00575663 04900593
  //   22C0006F 0057D663 04900593 2200006F 00E60663 04A00593 2140006F FD410113 00112023 00812223 00912423
  //   01212623 01312823 01412A23 01512C23 01612E23 03712023 03812223 03912423 00050413 00058493 00060913
  //   00068993 00078A13 00080A93 00400313 03230B33 00000B93 049BD663 00000C13 00098C93 034C5A63 00040513
  //   000C8593 00090613 00100693 000A0713 00000317 05C300E7 00AAA023 001C0C13 004C8C93 004A8A93 FD1FF06F
  //   001B8B93 01640433 FB9FF06F 00012083 00412403 00812483 00C12903 01012983 01412A03 01812A83 01C12B03
  //   02012B83 02412C03 02812C83 02C10113 00008067 FF410113 00112023 00812223 00912423 00050413 00060513
  //   00000317 068300E7 00058493 00068513 00070593 00000317 068300E7 00000513 00000293 00400393 02768333
  //   027703B3 02C2D263 00042E03 0004AE83 03DE0E33 01C50533 00640433 007484B3 00128293 FE1FF06F 00812483
  //   00412403 00012083 00C10113 00008067 00100293 00555663 04B00593 0B00006F 00008067 00100293 00555663
  //   04C00593 09C0006F 0055D663 04C00593 0900006F 00008067 00100293 0055D663 04D00593 07C0006F 00000293
  //   00400313 00100393 00052E03 02B3D263 02638EB3 01D50F33 000F2F83 01FE5663 00038293 000F8E13 00138393
  //   FE1FF06F 00028513 00008067 00100293 0055D663 04E00593 0300006F 00400293 00000313 02B30063 026283B3
  //   00750E33 000E2E83 000ED463 000E2023 00130313 FE5FF06F 00008067
  //   Instruction Memory
  //   Halts Execution After Constant # of Clock Cycles
  //   Constant
endmodule
