// Logisim project cpu-integration-test-proj2-dot.circ as structural Verilog: 1 circuit, main circuit run_main
module run_main (
  output [31:0] ra,
  output [31:0] sp,
  output [31:0] t0,
  output [31:0] t1,
  output [31:0] t2,
  output [31:0] s0,
  output [31:0] s1,
  output [31:0] a0,
  output [31:0] Requested_Address,
  output [31:0] Requested_Instruction,
  output [15:0] Time_Step,
  output halt
);

  wire clk;

  Clock clock_1 (.out(clk));
  // Probe on Requested_Address
  // test_harness test_harness_1: pin names not known; wires that end beside it: Requested_Instruction, clk, Requested_Address, ra, sp, t0, t1, t2, s0, s1, a0
  ROM #(.addrWidth(14), .dataWidth(32)) rom_1 (.addr(Requested_Address[15:2]), .data(Requested_Instruction));
  // Probe on Requested_Instruction
  Counter #(.max('hffff), .width(16)) counter_1 (.clk(clk), .Q(Time_Step));  // open: clr, load, up, count, D, carry
  Comparator #(.width(16)) comparator_1 (.a(Time_Step), .b(16'h5e), .eq(halt));  // open: gt, lt

  // Other names for the same wires on the sheet: fetch_addr[31:0] = Requested_Address;
  //   Instruction[31:0] = Requested_Instruction

  // Notes on the sheet:
  //   contents of rom_1 (hex, n*v repeats v):
  //   10437 ff040413 ff700293 542023 500293 542223 2440493 ffd00293 54a023 f00293 54a223 40513 48593
  //   300613 100693 100713 317 c300e7 b80006f ff410113 112023 812223 912423 50413 60513 317 68300e7 58493
  //   68513 70593 317 68300e7 513 293 400393 2768333 27703b3 2c2d263 42e03 4ae83 3de0e33 1c50533 640433
  //   7484b3 128293 fe1ff06f 812483 412403 12083 c10113 8067 100293 555663 4b00593 280006f 8067 100293
  //   555663 4c00593 140006f 55d663 4c00593 80006f 8067
  //   Instruction Memory
  //   Halts Execution After Constant # of Clock Cycles
  //   Constant
endmodule
